# Fritzing sketch smart-compass (saved by Fritzing 0.9.3b)
circuit board: 6cm x 7.8cm
breadboards: 1

parts:
  Sensor = Adafruit LSM9DS1 9DoF Breakout [part_number="Adafruit #3387"]
  SD = Adafruit MicroSD card breakout board [part_number="Adafruit #254"]
  Feather = Adafruit Feather M0 RFM9x LoRa [part_number="Adafruit #3178 or #3179"]
  Neopixel = Header 3 [package=screwterminal-3.5mm-3_lock.007s]
  GPS = Adafruit GPS FeatherWing [part_number="Adafruit #3133"]

nets:
  N1: Sensor.SDO_M, Sensor.SDO_AG, SD.DO, Feather.MISO
  N2: Sensor.CS_MAG, Feather.D12
  N3: Sensor.CS_AG, Feather.D11
  N4: Sensor.SDA, SD.DI, Feather.MOSI
  N5: Sensor.SCL, SD.CLK, Feather.SCK
  GND: Sensor.GND, SD.GND, Feather.GND, Neopixel.2, GPS.GND
  +3V3: Sensor.VIN, SD.+3V3, Feather.+3V3, Neopixel.3, GPS.3V
  N6: SD.CS, Feather.D10
  N7: Feather.D1, GPS.TX
  N8: Feather.D0, GPS.RX
  N9: Feather.D5, Neopixel.1

custom parts:
  Adafruit LSM9DS1 9DoF Breakout: Add motion, direction and orientation sensing to your Arduino project with this all-in-one 9-DOF sensor. Inside the chip are three sensors, one is a classic 3-axis accelerometer, which can tell you which direction is down towards the Earth (by measuring gravity) or how fast the board is accelerating in 3D space. The other is a 3-axis magnetometer that can sense where the strongest magnetic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
  Adafruit MicroSD card breakout board: Not just a simple breakout board, this microSD adapter goes the extra mile - designed for ease of use. Onboard 5v->3v regulator provides 150mA for power-hungry cards 3v level shifting means you can use this with ease on either 3v or 5v systems Uses a proper level shifting chip, not resistors: less problems, and faster read/write access Use 3 or 4 digital pins to read and write 2Gb+ of storage!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
  Adafruit Feather M0 RFM9x LoRa: This is the Adafruit Feather M0 RFM95 LoRa Radio - our take on an microcontroller with a "Long Range (LoRa)" packet radio transceiver with built in USB and battery charging. Its an Adafruit Feather M0 with a 433Mhz or 900MHz radio module cooked in! Great for making wireless networks that are more flexible than Bluetooth LE and without the high power requirements of WiFi. We have other boards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
  Adafruit GPS FeatherWing: Give your Feather a sense of place, with an Ultimate GPS FeatherWing. In 2013 we designed the Ultimate GPS module to satisfy all your GPS desires - and now we have brought its power and versatility plus more to our Feather series with the Adafruit Ultimate GPS FeatherWing! This FeatherWing plugs right into your Feather board and gives it a precise, sensitive, and low power GPS module for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

// code stored in the sketch: smart-compass.ino
#define DEBUG
#define DEBUG_SERIAL_WAIT
#include "bs_debug.h"
#define ARRAY_SIZE(array) ((sizeof(array)) / (sizeof(array[0])))

#include <AP_Declination.h>
#include <Adafruit_GPS.h>
#include <Adafruit_LSM9DS1.h>
#include <Adafruit_Sensor.h>
#include <EDB.h>
#include <FastLED.h>
#include <IniFile.h>
#include <RH_RF95.h>
#include <SD.h>
#include <SPI.h>
#include <Wire.h>
#include <elapsedMillis.h>
#include <pb_decode.h>
#include <pb_encode.h>

// it isn't legal for us to encrypt on amateur radio, but we need some sort of security so we sign our messages
// TODO: i think the code using this is broken and is causing crashes
#include <BLAKE2s.h>

#include "smart-compass.pb.h"
#include "types.h"

#define MAX_PINS 12

// TODO: was 77, but i think we need higher to keep the power usage down
#define LED_FADE_RATE 77

// Pins 0 and 1 are used for Serial1 (GPS)
#define RFM95_INT 3 // already wired for us
#define RFM95_RST 4 // already wired for us
#define LED_DATA 5
#define FLOATING_PIN 6
#define RFM95_CS 8      // already wired for us
#define VBAT_PIN 9      // already wired for us  // A7
#define SDCARD_CS 10
#define LSM9DS1_CSAG 11
#define LSM9DS1_CSM 12
#define RED_LED 13      // already wired for us
#define SPI_MISO 22     // shared between Radio+Sensors+SD
#define SPI_MOSI 23     // shared between Radio+Sensors+SD
#define SPI_SCK 24      // shared between Radio+Sensors+SD

#define gpsSerial Serial1

#define LED_CHIPSET NEOPIXEL

// lights for compass ring
const int inner_ring_size = 16;
const int inner_ring_start = 0;
const int inner_ring_end = inner_ring_start + inner_ring_size;

const int outer_ring_size = 24;
const int outer_ring_start = inner_ring_end;
const int outer_ring_end = outer_ring_start + outer_ring_size;

const int status_bar_size = 8;
const int status_bar_start = outer_ring_end;
const int status_bar_end = status_bar_start + status_bar_size;

const int num_LEDs = status_bar_end;
CRGB leds[num_LEDs];

// rotating "base color" used by some patterns
uint8_t g_hue = 0;

// the more peers, the longer it takes for peer data to update
const int max_peers = 4;

// setup messages for all possible peers
// TODO: pointers here? i think this is geting corrupted
SmartCompassLocationMessage compass_messages[max_peers] = {SmartCompassLocationMessage_init_default};

#define NETWORK_KEY_SIZE 16

// these are set by config
int my_peer_id, my_hue, my_saturation, num_peers;
uint8_t my_network_key[NETWORK_KEY_SIZE];

// these are set by config or fallback to defaults
int broadcast_time_s, default_brightness, flashlight_density, frames_per_second, gps_update_s, loop_delay_ms,
    min_peer_distance, max_peer_distance, ms_per_light_pattern, peer_led_ms, radio_power;

int time_zone_offset;

// it is not legal to encrypt in the US, but we can sign and hash for security
#define NETWORK_HASH_SIZE 16
BLAKE2s blake2s;
uint8_t my_network_hash[NETWORK_HASH_SIZE];

// offset between true and magnetic north
float g_magnetic_declination = 0.0;

// connect to the GPS
Adafruit_GPS GPS(&gpsSerial);

// save GPS data to SD card
// TODO: don't use String. use char array instead
String gps_log_filename = "";
File g_file;

// keep us from transmitting too often
long last_transmitted[max_peers] = {0};

bool config_setup, sd_setup, sensor_setup = false;

// TODO: these are getting overridden! i don't think these are declared how i need. i should be using pointers
CompassPin compass_pins[MAX_PINS];

int distance_sorted_compass_pin_ids[MAX_PINS];
int next_compass_pin = 0;

SmartCompassPinMessage pin_message_rx = SmartCompassPinMessage_init_default;
SmartCompassLocationMessage location_message_rx = SmartCompassLocationMessage_init_default;

SmartCompassPinMessage pin_message_tx = SmartCompassPinMessage_init_default;

const int max_compass_points = max_peers + 1;

// inner compass points go COUNTER-clockwise to match LEDs!
// TODO: this is wrong! this is not claiming the memory like i expected it to and setting this is breaking compass_pins
CHSV inner_compass_points[inner_ring_size][max_compass_points];
int next_inner_compass_point[inner_ring_size];

// TODO: initialize this?
CHSV outer_compass_points[outer_ring_size][max_compass_points];
int next_outer_compass_point[outer_ring_size];

// TODO: initialize this?
CHSV status_bar[status_bar_size];
int next_status_bar_id = 0;

elapsedMillis network_ms = 0;

int g_network_offset = 125 + 225;  // TODO: tune this. probably put it on the SD. tx takes 125ms.

BatteryStatus g_battery_status = BATTERY_FULL;

int g_packets_sent = 0;

const CHSV pin_colors[] PROGMEM = {
    // {h, s, v},
    // white
    {HUE_BLUE, 255, 255},
    {HUE_RED, 255, 255},   // Red for disabling, not for actual red pins!
    {HUE_YELLOW, 255, 255},
    {HUE_BLUE, 255, 255},
    {HUE_PINK, 128, 255},
};
int last_pin_color_id = 0;
const int delete_pin_color_id = 1;

const int max_points_per_color = 3;

void setupSPI() {
  // https://github.com/ImprobableStudios/Feather_TFT_LoRa_Sniffer/blob/9a8012ba316a652da669fe097c4b76c98bbaf35c/Feather_TFT_LoRa_Sniffer.ino#L222
  // The RFM95 has a pulldown on this pin, so the radio
  // is technically always selected unless you set the pin low.
  // this will cause other SPI devices to fail to function as
  // expected because CS (active-low) will be selected for
  // the RFM95 at the same time.
  digitalWrite(RFM95_CS, HIGH);

  digitalWrite(SDCARD_CS, HIGH);

  digitalWrite(LSM9DS1_CSM, HIGH);
  digitalWrite(LSM9DS1_CSAG, HIGH);

  // give everything time to wake up
  delay(200);

  SPI.begin();
}

void setup() {
  debug_serial(115200, 5000);

  DEBUG_PRINTLN("Setting up...");

  for (int i = 0; i < MAX_PINS; i++) {
    compass_pins[i].database_id = -1;
  }

  for (int i = 0; i < inner_ring_size; i++) {
    next_inner_compass_point[i] = 0;

    for (int j = 0; j < max_compass_points; j++) {
      inner_compass_points[i][j].hue = 128;
      inner_compass_points[i][j].saturation = 128;
      inner_compass_points[i][j].value = 128;
    }
  }

  for (int i = 0; i < outer_ring_size; i++) {
    next_outer_compass_point[i] = 0;

    for (int j = 0; j < max_compass_points; j++) {
      outer_compass_points[i][j].hue = 128;
      outer_compass_points[i][j].saturation = 128;
      outer_compass_points[i][j].value = 128;
    }
  }

  // TODO: something else is

  /*
  for (int i = 0; i < MAX_PINS; i++) {
    DEBUG_PRINTLN(compass_pins[i].database_id);
  }

  for (int i = 0; i < inner_ring_size; i++) {
    for (int j = 0; j < max_compass_points; j++) {
      DEBUG_PRINTLN(inner_compass_points[i][j].hue);
    }
  }

  for (int i = 0; i < outer_ring_size; i++) {
    for (int j = 0; j < max_compass_points; j++) {
      DEBUG_PRINTLN(outer_compass_points[i][j].hue);
    }
  }
  */

  // Configure SPI pins for everything BEFORE trying to do anything with them individually
  setupSPI();

  checkBattery(&g_battery_status);

  randomSeed(analogRead(FLOATING_PIN));

  // configuration depends on SD card so do it first
  setupSD();

  setupConfig();

  setupLights();

  // do more setup now that we have our configuration
  if (config_setup) {
    setupGPS();
    setupRadio();
  }

  setupSensor();

  // open the SD card
  g_file = SD.open(gps_log_filename, FILE_WRITE);

  // if the file opened okay, write to it:
  if (!g_file) {
    // if the file didn't open, print an error and abort
    DEBUG_PRINT(F("error opening gps log: "));
    DEBUG_PRINTLN(gps_log_filename);
  } else {
    DEBUG_PRINT(F("Logging start to "));
    DEBUG_PRINTLN(gps_log_filename);

    // add a blank line each time we start
    g_file.println("");

    // close the file:
    g_file.close();
  }

  // TODO: load saved locations

  // configure the timer that reads GPS data to run at <sampleRate>Hertz
  tcConfigure(10);
  tcStartCounter();

  if (sd_setup) {
    loadCompassPins();
  }

  DEBUG_PRINTLN(F("Starting..."));
}

/*
 * this stuff was in its own .ino files, but something was broken about it
 * i think i fixed it by moving the struct definitions to types.h, but I'm not sure how best to move g_file and db defs
 */

#define TABLE_SIZE 4096 * 2

// The max number of records that should be created = (TABLE_SIZE - sizeof(EDB_Header)) / sizeof(LogEvent).
// If you try to insert more, operations will return EDB_OUT_OF_RANGE for all records outside the usable range.

const char *db_name = "compass.db";

// The read and write handlers for using the SD Library
// Also blinks the led while writing/reading
// database entries start at 1!
inline void writer(unsigned long address, const byte *data, unsigned int recsize) {
  digitalWrite(RED_LED, HIGH);
  g_file.seek(address);
  g_file.write(data, recsize);
  g_file.flush();
  digitalWrite(RED_LED, LOW);
}

inline void reader(unsigned long address, byte *data, unsigned int recsize) {
  digitalWrite(RED_LED, HIGH);
  g_file.seek(address);
  g_file.read(data, recsize);
  digitalWrite(RED_LED, LOW);
}

// Create an EDB object with the appropriate write and read handlers
// NOTE! These handlers do NOT open or close the database file!
EDB db(&writer, &reader);

/*
 * END things that should be moved into their own ino files
 */

unsigned int g_time_segment_id = 99;
unsigned int g_broadcasting_peer_id = 99;
unsigned int g_broadcasted_peer_id = 99;
Orientation g_current_orientation;

void loop() {
  // each peer needs enough time to broadcast data for every other peer.
  // TODO: then double the number of time segments so we can spend half the time sleeping
  static const unsigned int time_segments = num_peers * num_peers;
  static unsigned int time_segment_id, broadcasting_peer_id, broadcasted_peer_id;
  static unsigned long gps_time = 0;

  if (config_setup) {
    // decrease overall brightness if battery is low
    // TODO: how often should we do this?
    EVERY_N_SECONDS(300) {
      checkBattery(&g_battery_status);

      // TODO: only do this if the battery level has changed. (unless callign setBrightness is cheap?)
      // TODO: set a floor on these
      switch (g_battery_status) {
      case BATTERY_DEAD:
        // TODO: use map_float(quadwave8(millis()), 0, 256, 0.3, 0.5);
        // TODO: maybe add a red led to a strip of 8 LEDs?
        FastLED.setBrightness(default_brightness * .5);
        break;
      case BATTERY_LOW:
        FastLED.setBrightness(default_brightness * .75);
        break;
      case BATTERY_OK:
        FastLED.setBrightness(default_brightness * .90);
        break;
      case BATTERY_FULL:
        // TODO: different light pattern instead?
        FastLED.setBrightness(default_brightness);
        break;
      }
    }

    /*
    EVERY_N_SECONDS(10) {
      // TODO: print peer location data
    }
    */

    EVERY_N_MILLISECONDS(1000 / frames_per_second) {
      getOrientation(&g_current_orientation);
    }

    gpsReceive();

    updateLights(16);

    if (GPS.fix) {
      getGPSTime(&gps_time);

      time_segment_id = (gps_time / broadcast_time_s) % time_segments;

      broadcasting_peer_id = time_segment_id / num_peers;
      broadcasted_peer_id = time_segment_id % num_peers;

      // DEBUG
      g_time_segment_id = time_segment_id;
      g_broadcasting_peer_id = broadcasting_peer_id;
      g_broadcasted_peer_id = broadcasted_peer_id;
      // END DEBUG

      if (broadcasting_peer_id == my_peer_id) {
        // TODO: trying to figure out where the crash is. i think its in here
        radioTransmit(broadcasted_peer_id);
      } else if (broadcasting_peer_id >= num_peers) {
        // spend 1/2 the time with the radio sleeping
        radioSleep();
      } else {
        radioReceive();
      }
    } else {
      // even if we don't have a GPS fix, we can still update peer locations
      // this will take more power since the GPS will be searching for a fix and the radio will be on
      radioReceive();
    }

    // transmitting can be slow. update lights again just in case
    //updateLights(17);
  } else {
    // without config, we can't do anything with radios or saved GPS locations. just do the lights
    updateLights(18);
  }

  // don't sleep too long or you get in the way of radios. keep this less < framerate
  FastLED.delay(loop_delay_ms);
}
